// Digital circuit projekt.dig as structural Verilog
module projekt (
  input  clk,
  input  I1,
  input  I2
);

  wire and_1_out, and_2_out, and_3_out, and_4_out, and_5_out, and_6_out, and_7_out, and_8_out, and_9_out,
       and_10_out, and_11_out, and_12_out, and_13_out, and_14_out, and_15_out, and_16_out, d_ff_1_nq,
       d_ff_1_q, d_ff_2_nq, d_ff_2_q, not_1_out, not_2_out, or_1_out, or_2_out, or_3_out, or_4_out, or_5_out;

  not not_1 (not_1_out, I1);
  not not_2 (not_2_out, I2);
  and and_1 (and_1_out, d_ff_2_nq, I1);
  or or_1 (or_1_out, and_2_out, and_1_out);
  LED led_1 (.in(or_1_out));
  and and_2 (and_2_out, d_ff_1_nq, d_ff_2_nq);
  and and_3 (and_3_out, d_ff_2_nq, not_2_out, I1);
  and and_4 (and_4_out, d_ff_1_q, d_ff_2_q, I2);
  or or_2 (or_2_out, and_6_out, and_5_out, and_4_out, and_3_out);
  LED led_2 (.in(or_2_out));
  and and_5 (and_5_out, not_2_out, d_ff_1_nq, d_ff_2_q, not_1_out);
  and and_6 (and_6_out, d_ff_1_nq, d_ff_2_nq, I1);
  and and_7 (and_7_out, d_ff_2_nq, not_2_out, I1);
  and and_8 (and_8_out, d_ff_1_q, I1, d_ff_2_nq);
  or or_3 (or_3_out, and_10_out, and_9_out, and_8_out, and_7_out);
  LED led_3 (.in(or_3_out));
  and and_9 (and_9_out, d_ff_1_q, not_2_out, d_ff_2_nq);
  and and_10 (and_10_out, d_ff_1_nq, d_ff_2_q, I2);
  and and_11 (and_11_out, d_ff_2_q, I2, I1);
  and and_12 (and_12_out, d_ff_2_nq, not_2_out, I1);
  LED led_4 (.in(or_4_out));
  and and_13 (and_13_out, not_1_out, d_ff_1_q, d_ff_2_q, not_2_out);
  or or_4 (or_4_out, and_14_out, and_13_out, and_12_out, and_11_out);
  and and_14 (and_14_out, d_ff_1_q, d_ff_2_nq, I2, not_1_out);
  and and_15 (and_15_out, d_ff_2_q, d_ff_1_nq);
  D_FF d_ff_1 (.D(or_5_out), .C(clk), .Q(d_ff_1_q), .nQ(d_ff_1_nq));
  and and_16 (and_16_out, d_ff_2_nq, d_ff_1_q);
  or or_5 (or_5_out, and_16_out, and_15_out);
  D_FF d_ff_2 (.D(d_ff_2_nq), .C(clk), .Q(d_ff_2_q), .nQ(d_ff_2_nq));
endmodule
