// Digital circuit projekt.dig as structural Verilog
module projekt (
  input  clk
);

  wire and_1_out, and_2_out, and_3_out, and_4_out, and_5_out, and_6_out, and_7_out, and_8_out, and_9_out,
       and_10_out, and_11_out, and_12_out, and_13_out, and_14_out, and_15_out, and_16_out, button_1_out,
       d_ff_1_nq, d_ff_1_q, d_ff_2_nq, d_ff_2_q, jk_ff_1_q, jk_ff_2_q, not_1_out, not_2_out, not_3_out,
       not_4_out, or_1_out, or_2_out, or_3_out, or_4_out, or_5_out;

  Button button_1 (.out(button_1_out));
  not not_1 (not_1_out, button_1_out);
  JK_FF jk_ff_1 (.J(1'b1), .C(not_1_out), .K(1'b1), .Q(jk_ff_1_q));  // open: nQ
  not not_2 (not_2_out, jk_ff_1_q);
  JK_FF jk_ff_2 (.J(1'b1), .C(not_2_out), .K(1'b1), .Q(jk_ff_2_q));  // open: nQ
  not not_3 (not_3_out, jk_ff_2_q);
  not not_4 (not_4_out, jk_ff_1_q);
  and and_1 (and_1_out, d_ff_2_nq, jk_ff_2_q);
  or or_1 (or_1_out, and_2_out, and_1_out);
  LED led_1 (.in(or_1_out));
  and and_2 (and_2_out, d_ff_1_nq, d_ff_2_nq);
  and and_3 (and_3_out, d_ff_2_nq, not_4_out, jk_ff_2_q);
  and and_4 (and_4_out, d_ff_1_q, d_ff_2_q, jk_ff_1_q);
  or or_2 (or_2_out, and_6_out, and_5_out, and_4_out, and_3_out);
  LED led_2 (.in(or_2_out));
  and and_5 (and_5_out, not_4_out, d_ff_1_nq, d_ff_2_q, not_3_out);
  and and_6 (and_6_out, d_ff_1_nq, d_ff_2_nq, jk_ff_2_q);
  and and_7 (and_7_out, d_ff_2_nq, not_4_out, jk_ff_2_q);
  and and_8 (and_8_out, d_ff_1_q, jk_ff_2_q, d_ff_2_nq);
  or or_3 (or_3_out, and_10_out, and_9_out, and_8_out, and_7_out);
  LED led_3 (.in(or_3_out));
  and and_9 (and_9_out, d_ff_1_q, not_4_out, d_ff_2_nq);
  and and_10 (and_10_out, d_ff_1_nq, d_ff_2_q, jk_ff_1_q);
  and and_11 (and_11_out, d_ff_2_q, jk_ff_1_q, jk_ff_2_q);
  and and_12 (and_12_out, d_ff_2_nq, not_4_out, jk_ff_2_q);
  LED led_4 (.in(or_4_out));
  and and_13 (and_13_out, not_3_out, d_ff_1_q, d_ff_2_q, not_4_out);
  or or_4 (or_4_out, and_14_out, and_13_out, and_12_out, and_11_out);
  and and_14 (and_14_out, d_ff_1_q, d_ff_2_nq, jk_ff_1_q, not_3_out);
  and and_15 (and_15_out, d_ff_2_q, d_ff_1_nq);
  D_FF d_ff_1 (.D(or_5_out), .C(clk), .Q(d_ff_1_q), .nQ(d_ff_1_nq));
  and and_16 (and_16_out, d_ff_2_nq, d_ff_1_q);
  or or_5 (or_5_out, and_16_out, and_15_out);
  D_FF d_ff_2 (.D(d_ff_2_nq), .C(clk), .Q(d_ff_2_q), .nQ(d_ff_2_nq));
endmodule
